# Fritzing sketch truck (saved by Fritzing 0.8.3b)
circuit board: 16.9333cm x 5.64444cm
breadboards: 1

parts:
  Part1 = Arduino Uno (Rev3)
  Q1 = NPN-Transistor [package="TO92 [THT]"]
  Q2 = NPN-Transistor [package="TO92 [THT]"]
  Q3 = NPN-Transistor [package="TO92 [THT]"]
  LED2 = LED - 5mm [color="White (6500K)" package="5 mm [THT]"]
  LED3 = LED - 5mm [color="Yellow (592nm)" package="5 mm [THT]"]
  VCC1 = 4 x AAA Battery Mount
  S1 = Pushbutton [package="[THT]"]
  S2 = Pushbutton [package="[THT]"]
  S3 = Pushbutton [package="[THT]"]
  R5 = Resistor [tolerance=±5% resistance=100k package=THT]
  R6 = Resistor [tolerance=±5% resistance=100k package=THT]
  R7 = Resistor [tolerance=±5% resistance=100k package=THT]
  LED4 = LED - 5mm [color="Yellow (595nm)" package="5 mm [THT]"]
  LED5 = LED - 5mm [color="Red (633nm)" package="5 mm [THT]"]
  LED6 = LED - 5mm [color="Red (633nm)" package="5 mm [THT]"]
  R9 = Resistor [tolerance=±5% resistance=47 package=THT]
  LED7 = LED - 5mm [color="White (6500K)" package="5 mm [THT]"]
  R10 = Resistor [tolerance=±5% resistance=47 package=THT]
  LED8 = LED - 5mm [color="Red (633nm)" package="5 mm [THT]"]
  LED9 = LED - 5mm [color="Red (633nm)" package="5 mm [THT]"]
  LED10 = LED - 5mm [color="Yellow (595nm)" package="5 mm [THT]"]
  LED11 = LED - 5mm [color="Yellow (592nm)" package="5 mm [THT]"]
  LED12 = LED - 5mm [color="Red (633nm)" package="5 mm [THT]"]
  LED13 = LED - 5mm [color="Red (633nm)" package="5 mm [THT]"]
  LED14 = LED - 5mm [color="Red (633nm)" package="5 mm [THT]"]
  LED15 = LED - 5mm [color="Red (633nm)" package="5 mm [THT]"]
  R12 = Resistor [tolerance=±5% resistance=100 package=THT]
  R14 = Resistor [tolerance=±5% resistance=3.3 package=THT]

nets (from the schematic view):
  N1: Part1.ICSP_MISO, Part1.D12/MISO, Q2.B
  N2: Part1.ICSP_SCK, Q3.B
  N3: Part1.ICSP_MOSI, Part1.D11_PWM/MOSI, Q1.B
  N4: Part1.GND, LED2.cathode, LED3.cathode, VCC1.-, R5.Pin_0, R6.Pin_0, R7.Pin_0, LED6.cathode, LED7.cathode, LED8.cathode, LED11.cathode, LED12.cathode, LED13.cathode
  N5: Part1.D5_PWM, S1.Pin_3, S1.Pin_4, R7.Pin_1
  N6: Part1.D6_PWM, S2.Pin_3, S2.Pin_4, R6.Pin_1
  N7: Part1.D7, S3.Pin_3, S3.Pin_4, R5.Pin_1
  N8: Part1.3V3, S1.Pin_1, S1.Pin_2, S2.Pin_1, S2.Pin_2, S3.Pin_1, S3.Pin_2
  N9: Q1.E, R9.Pin_0
  N10: Q2.E, R10.Pin_0
  N11: Q2.C, Q3.C, VCC1.+
  N12: Q3.E, R12.Pin_0, R14.Pin_0
  N13: LED2.anode, LED7.anode, R14.Pin_1
  N14: LED3.anode, LED4.cathode
  N15: LED4.anode, LED5.anode, R9.Pin_1
  N16: LED5.cathode, LED6.anode
  N17: R10.Pin_1, LED9.anode, LED10.anode
  N18: LED8.anode, LED9.cathode
  N19: LED10.cathode, LED11.anode
  N20: LED12.anode, LED15.cathode
  N21: LED13.anode, LED14.cathode
  N22: LED14.anode, LED15.anode, R12.Pin_1
